// Logisim project P3.circ as structural Verilog: 15 circuits, main circuit grf_2reg
module grf_2reg (
  input  clk,
  input  reset,
  input  WE,
  input  A1,
  input  A2,
  input  A3,
  input  [31:0] WD,
  output [31:0] RD1,
  output [31:0] RD2
);

  wire A3_0, A3_1, and_1_out, and_2_out;
  wire [31:0] out0, out1;

  Decoder decoder_1 (.out0(A3_0), .out1(A3_1), .sel(A3));  // open: en
  and and_1 (and_1_out, A3_0, WE);
  and and_2 (and_2_out, A3_1, WE);
  Register #(.width(32)) _0 (.D(WD), .en(and_1_out), .Q(out0), .clk(clk), .clr(reset));
  Register #(.width(32)) _1 (.D(WD), .en(and_2_out), .Q(out1), .clk(clk), .clr(reset));
  Multiplexer #(.width(32)) multiplexer_1 (.in0(out0), .in1(out1), .out(RD1), .sel(A1));  // open: en
  Multiplexer #(.width(32)) multiplexer_2 (.in0(out0), .in1(out1), .out(RD2), .sel(A2));  // open: en

  // Other names for the same wires on the sheet: res = reset
endmodule

module grf_4reg (
  input  clk,
  input  reset,
  input  WE,
  input  [1:0] A1,
  input  [1:0] A2,
  input  [1:0] A3,
  input  [31:0] WD,
  output [31:0] RD1,
  output [31:0] RD2
);

  wire A31_0, A31_1, and_1_out, and_2_out;
  wire [31:0] out10, out11, out20, out21;

  Decoder decoder_1 (.out0(A31_0), .out1(A31_1), .sel(A3[1]));  // open: en
  and and_1 (and_1_out, WE, A31_0);
  grf_2reg grf_2reg_1 (
    .A1(A1[0]), .A2(A2[0]), .A3(A3[0]), .WD(WD), .RD1(out10), .RD2(out20), .clk(clk), .reset(reset),
    .WE(and_1_out));
  and and_2 (and_2_out, WE, A31_1);
  grf_2reg grf_2reg_2 (
    .A1(A1[0]), .A2(A2[0]), .A3(A3[0]), .WD(WD), .RD1(out11), .RD2(out21), .clk(clk), .reset(reset),
    .WE(and_2_out));
  Multiplexer #(.width(32)) multiplexer_1 (.in0(out10), .in1(out11), .out(RD1), .sel(A1[1]));  // open: en
  Multiplexer #(.width(32)) multiplexer_2 (.in0(out20), .in1(out21), .out(RD2), .sel(A2[1]));  // open: en

  // Other names for the same wires on the sheet: res = reset
endmodule

module grf_8reg (
  input  clk,
  input  reset,
  input  WE,
  input  [2:0] A1,
  input  [2:0] A2,
  input  [2:0] A3,
  input  [31:0] WD,
  output [31:0] RD1,
  output [31:0] RD2
);

  wire A31_0, A31_1, and_1_out, and_2_out;
  wire [31:0] out10, out11, out20, out21;

  Decoder decoder_1 (.out0(A31_0), .out1(A31_1), .sel(A3[2]));  // open: en
  and and_1 (and_1_out, WE, A31_0);
  grf_4reg grf_4reg_1 (
    .A1(A1[1:0]), .A2(A2[1:0]), .A3(A3[1:0]), .WD(WD), .clk(clk), .reset(reset), .WE(and_1_out), .RD1(out10),
    .RD2(out20));
  and and_2 (and_2_out, WE, A31_1);
  grf_4reg grf_4reg_2 (
    .A1(A1[1:0]), .A2(A2[1:0]), .A3(A3[1:0]), .WD(WD), .clk(clk), .reset(reset), .WE(and_2_out), .RD1(out11),
    .RD2(out21));
  Multiplexer #(.width(32)) multiplexer_1 (.in0(out10), .in1(out11), .out(RD1), .sel(A1[2]));  // open: en
  Multiplexer #(.width(32)) multiplexer_2 (.in0(out20), .in1(out21), .out(RD2), .sel(A2[2]));  // open: en

  // Other names for the same wires on the sheet: A10[1:0] = A1[1:0]; A11 = A1[2]; A20[1:0] = A2[1:0]; A21 = A2[2];
  //   A30[1:0] = A3[1:0]; A31 = A3[2]; res = reset
endmodule

module grf_16reg (
  input  clk,
  input  reset,
  input  WE,
  input  [3:0] A1,
  input  [3:0] A2,
  input  [3:0] A3,
  input  [31:0] WD,
  output [31:0] RD1,
  output [31:0] RD2
);

  wire A31_0, A31_1, and_1_out, and_2_out;
  wire [31:0] out10, out11, out20, out21;

  Decoder decoder_1 (.out0(A31_0), .out1(A31_1), .sel(A3[3]));  // open: en
  and and_1 (and_1_out, WE, A31_0);
  grf_8reg grf_8reg_1 (
    .A1(A1[2:0]), .A2(A2[2:0]), .A3(A3[2:0]), .WD(WD), .clk(clk), .reset(reset), .WE(and_1_out), .RD1(out10),
    .RD2(out20));
  and and_2 (and_2_out, WE, A31_1);
  grf_8reg grf_8reg_2 (
    .A1(A1[2:0]), .A2(A2[2:0]), .A3(A3[2:0]), .WD(WD), .clk(clk), .reset(reset), .WE(and_2_out), .RD1(out11),
    .RD2(out21));
  Multiplexer #(.width(32)) multiplexer_1 (.in0(out10), .in1(out11), .out(RD1), .sel(A1[3]));  // open: en
  Multiplexer #(.width(32)) multiplexer_2 (.in0(out20), .in1(out21), .out(RD2), .sel(A2[3]));  // open: en

  // Other names for the same wires on the sheet: A10[2:0] = A1[2:0]; A11 = A1[3]; A20[2:0] = A2[2:0]; A21 = A2[3];
  //   A30[2:0] = A3[2:0]; A31 = A3[3]; res = reset
endmodule

module grf_32reg (
  input  clk,
  input  reset,
  input  WE,
  input  [4:0] A1,
  input  [4:0] A2,
  input  [4:0] A3,
  input  [31:0] WD,
  output [31:0] RD1,
  output [31:0] RD2
);

  wire A31_0, A31_1, and_1_out, and_2_out;
  wire [31:0] out10, out11, out20, out21;

  Decoder decoder_1 (.out0(A31_0), .out1(A31_1), .sel(A3[4]));  // open: en
  and and_1 (and_1_out, WE, A31_0);
  grf_16reg grf_16reg_1 (
    .A1(A1[3:0]), .A2(A2[3:0]), .A3(A3[3:0]), .WD(WD), .clk(clk), .reset(reset), .WE(and_1_out), .RD1(out10),
    .RD2(out20));
  and and_2 (and_2_out, WE, A31_1);
  grf_16reg grf_16reg_2 (
    .A1(A1[3:0]), .A2(A2[3:0]), .A3(A3[3:0]), .WD(WD), .clk(clk), .reset(reset), .WE(and_2_out), .RD1(out11),
    .RD2(out21));
  Multiplexer #(.width(32)) multiplexer_1 (.in0(out10), .in1(out11), .out(RD1), .sel(A1[4]));  // open: en
  Multiplexer #(.width(32)) multiplexer_2 (.in0(out20), .in1(out21), .out(RD2), .sel(A2[4]));  // open: en

  // Other names for the same wires on the sheet: A10[3:0] = A1[3:0]; A11 = A1[4]; A20[3:0] = A2[3:0]; A21 = A2[4];
  //   A30[3:0] = A3[3:0]; A31 = A3[4]; res = reset
endmodule

module GRF (
  input  clk,
  input  reset,
  input  WE,
  input  [4:0] A1,
  input  [4:0] A2,
  input  [4:0] A3,
  input  [31:0] WD,
  output [31:0] RD1,
  output [31:0] RD2
);

  wire comparator_1_eq;
  wire [31:0] WD_t;

  Comparator #(.width(5)) comparator_1 (.a({5{1'b0}}), .b(A3), .eq(comparator_1_eq));  // open: gt, lt
  Multiplexer #(.width(32)) multiplexer_1 (.in0(WD), .in1({32{1'b0}}), .out(WD_t), .sel(comparator_1_eq));  // open: en
  grf_32reg grf_32reg_1 (.A1(A1), .A2(A2), .A3(A3), .WD(WD_t), .clk(clk), .reset(reset), .WE(WE), .RD1(RD1), .RD2(RD2));

  // Other names for the same wires on the sheet: res = reset
endmodule

module main (
  input  reset,
  output [31:0] Instr,
  output [31:0] pc,
  output RegWrite,
  output [4:0] RegAddr,
  output [31:0] RegData,
  output MemWrite,
  output [31:0] MemAddr,
  output [31:0] MemData
);

  wire alu_1_zero, ALUSrc, branch, branch_t, clk, ExtOp, MemtoReg, RegDst;
  wire [2:0] ALUctr;
  wire [15:0] bit_extender_1_out;
  wire [31:0] dm_1_rd, ext_1_imm32, grf_1_rd1, multiplexer_3_out, npc_1_pc_prime;

  Clock u_clk (.out(clk));
  NPC npc_1 (.PC(pc), .imm(Instr[15:0]), .branch(branch), .PC_prime(npc_1_pc_prime));
  // Probe on Instr[31:26]
  // Probe on Instr[15:0]
  // Probe on Instr[25:21]
  // Probe on Instr[20:16]
  // Probe on Instr[15:11]
  // Probe on Instr[10:6]
  // Probe on Instr[5:0]
  Controller controller_1 (
    .RegDst(RegDst), .ALUSrc(ALUSrc), .MemtoRed(MemtoReg), .RegWrite(RegWrite), .MemWrute(MemWrite),
    .branch(branch_t), .ExtOp(ExtOp), .ALUctr(ALUctr), .op(Instr[31:26]), .func(Instr[5:0]));
  IFU ifu_1 (.PC_prime(npc_1_pc_prime), .clk(clk), .rst(reset), .Instr(Instr), .PC(pc));
  Multiplexer #(.width(5)) multiplexer_1 (
    .in0(Instr[20:16]), .in1(Instr[15:11]), .out(RegAddr), .sel(RegDst));  // open: en
  Bit_Extender #(.in_width(32)) bit_extender_1 (.in(MemAddr), .out(bit_extender_1_out));
  GRF grf_1 (
    .A1(Instr[25:21]), .A2(Instr[20:16]), .A3(RegAddr), .WD(RegData), .RD1(grf_1_rd1), .RD2(MemData),
    .clk(clk), .reset(reset), .WE(RegWrite));
  DM dm_1 (.A(bit_extender_1_out), .WD(MemData), .RD(dm_1_rd), .clk(clk), .reset(reset), .WE(MemWrite));
  EXT ext_1 (.imm(Instr[15:0]), .ExtOp(ExtOp), .imm32(ext_1_imm32));
  Multiplexer #(.width(32)) multiplexer_2 (.in0(MemAddr), .in1(dm_1_rd), .out(RegData), .sel(MemtoReg));  // open: en
  ALU alu_1 (.ALUResult(MemAddr), .Op1(grf_1_rd1), .Op2(multiplexer_3_out), .ALUControl(ALUctr), .Zero(alu_1_zero));
  Multiplexer #(.width(32)) multiplexer_3 (
    .in0(MemData), .in1(ext_1_imm32), .out(multiplexer_3_out), .sel(ALUSrc));  // open: en
  // Probe on MemAddr
  and and_1 (branch, alu_1_zero, branch_t);

  // Other names for the same wires on the sheet: ALUResult[31:0] = MemAddr; func[5:0] = Instr[5:0];
  //   off_imm[15:0] = Instr[15:0]; shamt[4:0] = Instr[10:6]; rd[4:0] = Instr[15:11]; rt_t[4:0] = Instr[20:16];
  //   rs[4:0] = Instr[25:21]; op[5:0] = Instr[31:26]; rt[31:0] = MemData; WD[31:0] = RegData
endmodule

module IFU (
  input  [31:0] PC_prime,
  input  clk,
  input  rst,
  output [31:0] Instr,
  output [31:0] PC
);

  wire counter_1_q;
  wire [31:0] multiplexer_1_out, subtractor_1_out;

  Multiplexer #(.width(32)) multiplexer_1 (
    .in0(32'h3000), .in1(PC_prime), .out(multiplexer_1_out), .sel(counter_1_q));  // open: en
  Counter #(.width(1), .max('h1), .ongoal("stay")) counter_1 (
    .Q(counter_1_q), .clk(clk), .clr(rst));  // open: load, D, count, carry
  Register #(.width(32)) u_PC (.D(multiplexer_1_out), .Q(PC), .clk(clk), .clr(rst));  // open: en
  Subtractor #(.width(32)) subtractor_1 (.a(PC), .b(32'h3000), .out(subtractor_1_out));  // open: bin, bout
  ROM #(.addrWidth(12), .dataWidth(32)) rom_1 (.addr(subtractor_1_out[13:2]), .data(Instr));  // open: sel

  // Notes on the sheet:
  //   IM
  //   contents of rom_1 (hex, n*v repeats v):
  //   3404007b 348501c8 3c06007b 3c07ffff 34e7ffff 868020 878820 e79020 34080000 ad040000 ad050004
  //   ad060008 ad07000c ad100010 ad110014 ad120018 8d040000 8d05000c ad04001c ad050020 34040001 34050002
  //   34060001 10850001 10860001 ad040024 ad050028
endmodule

module ALU (
  input  [31:0] Op1,
  input  [31:0] Op2,
  input  [2:0] ALUControl,
  output [31:0] ALUResult,
  output Zero
);

  wire comparator_1_lt;
  wire [31:0] adder_1_out, bit_extender_1_out, or_1_out, shifter_1_out, subtractor_1_out;

  Adder #(.width(32)) adder_1 (.a(Op1), .b(Op2), .out(adder_1_out));  // open: cin, cout
  Subtractor #(.width(32)) subtractor_1 (.a(Op1), .b(Op2), .out(subtractor_1_out));  // open: bin, bout
  assign or_1_out = Op1 | Op2;  // OR_Gate or_1, 32 bits wide
  Comparator #(.width(32), .mode("unsigned")) comparator_1 (.a(Op1), .b(Op2), .lt(comparator_1_lt));  // open: gt, eq
  Shifter #(.width(32)) shifter_1 (.in(Op2), .\dist (5'b10000), .out(shifter_1_out));
  assign bit_extender_1_out = {{31{1'b0}}, comparator_1_lt};  // Bit_Extender bit_extender_1
  Multiplexer #(.select(3), .width(32)) multiplexer_1 (
    .in0(adder_1_out), .in1(subtractor_1_out), .in2(or_1_out), .in3(bit_extender_1_out), .in4(shifter_1_out),
    .out(ALUResult), .sel(ALUControl));  // open: in5, in6, in7, en
  Comparator #(.width(32), .mode("unsigned")) comparator_2 (.a(ALUResult), .b({32{1'b0}}), .eq(Zero));  // open: gt, lt
endmodule

module andLogic (
  input  op5,
  input  op4,
  input  op3,
  input  op2,
  input  op1,
  input  op0,
  input  func5,
  input  func4,
  input  func3,
  input  func2,
  input  func1,
  input  func0,
  output add,
  output ori,
  output sub,
  output lw,
  output nop,
  output sw,
  output beq,
  output lui
);

  wire a_s_n, not_1_out, not_2_out, not_3_out, not_4_out, not_5_out, not_6_out, not_7_out, not_8_out,
       not_9_out, not_10_out, not_11_out, not_12_out;

  not not_1 (not_1_out, op5);
  not not_2 (not_2_out, op4);
  not not_3 (not_3_out, op2);
  not not_4 (not_4_out, op3);
  not not_5 (not_5_out, op0);
  not not_6 (not_6_out, op1);
  and u_a_s_n (a_s_n, not_1_out, not_2_out, not_4_out, not_3_out, not_6_out, not_5_out);
  and u_ori (ori, not_1_out, not_2_out, op3, op2, not_6_out, op0);
  and u_lw (lw, op5, not_2_out, not_4_out, not_3_out, op1, op0);
  and u_sw (sw, op5, not_2_out, op3, not_3_out, op1, op0);
  and u_beq (beq, not_1_out, not_2_out, not_4_out, op2, not_6_out, not_5_out);
  and u_lui (lui, not_1_out, not_2_out, op3, op2, op1, op0);
  not not_7 (not_7_out, func5);
  not not_8 (not_8_out, func4);
  not not_9 (not_9_out, func3);
  not not_10 (not_10_out, func2);
  not not_11 (not_11_out, func1);
  not not_12 (not_12_out, func0);
  and u_add (add, a_s_n, func5, not_8_out, not_9_out, not_10_out, not_11_out, not_12_out);
  and u_sub (sub, a_s_n, func5, not_8_out, not_9_out, not_10_out, func1, not_12_out);
  and u_nop (nop, a_s_n, not_7_out, not_8_out, not_9_out, not_10_out, not_11_out, not_12_out);
endmodule

module DM (
  input  clk,
  input  reset,
  input  WE,
  input  [15:0] A,
  input  [31:0] WD,
  output [31:0] RD
);

  wire [9:0] A00, A01, A10;
  wire [31:0] ram_1_data, ram_2_data, ram_3_data;

  Demultiplexer #(.select(2), .width(10)) demultiplexer_1 (
    .out0(A00), .out1(A01), .out2(A10), .in(A[11:2]), .sel(A[13:12]));  // open: out3, en
  RAM #(.addrWidth(10), .dataWidth(32), .bus("separate")) ram_1 (
    .addr(A00), .din(WD), .data(ram_1_data), .str(WE), .clk(clk), .clr(reset));  // open: sel, ld
  RAM #(.addrWidth(10), .dataWidth(32), .bus("separate")) ram_2 (
    .addr(A01), .din(WD), .data(ram_2_data), .str(WE), .clk(clk), .clr(reset));  // open: sel, ld
  RAM #(.addrWidth(10), .dataWidth(32), .bus("separate")) ram_3 (
    .addr(A10), .din(WD), .data(ram_3_data), .str(WE), .clk(clk), .clr(reset));  // open: sel, ld
  Multiplexer #(.select(2), .width(32)) multiplexer_1 (
    .in0(ram_1_data), .in1(ram_2_data), .in2(ram_3_data), .out(RD), .sel(A[13:12]));  // open: in3, en

  // Other names for the same wires on the sheet: A_t[9:0] = A[11:2]; sel[1:0] = A[13:12]; res = reset
endmodule

module EXT (
  input  [15:0] imm,
  input  ExtOp,
  output [31:0] imm32
);

  wire [31:0] bit_extender_1_out, bit_extender_2_out;

  assign bit_extender_1_out = {{16{1'b0}}, imm};  // Bit_Extender bit_extender_1
  Multiplexer #(.width(32)) multiplexer_1 (
    .in0(bit_extender_1_out), .in1(bit_extender_2_out), .out(imm32), .sel(ExtOp));  // open: en
  assign bit_extender_2_out = {{16{imm[15]}}, imm};  // Bit_Extender bit_extender_2
endmodule

module orLogic (
  input  add,
  input  sub,
  input  ori,
  input  lw,
  input  sw,
  input  beq,
  input  lui,
  input  nop,
  output RegDst,
  output ALUSrc,
  output MemtoRed,
  output RegWrite,
  output MemWrute,
  output branch,
  output ExtOp,
  output [2:0] ALUctr
);

  or or_1 (RegDst, add, sub);
  or or_2 (ALUSrc, ori, lw, sw, lui);
  buf or_3 (MemtoRed, lw);  // OR_Gate
  or or_4 (RegWrite, add, sub, ori, lw, lui);
  buf or_5 (MemWrute, sw);  // OR_Gate
  buf or_6 (branch, beq);  // OR_Gate
  or or_7 (ExtOp, lw, sw, beq);
  or or_8 (ALUctr[0], sub, beq);
  buf or_9 (ALUctr[1], ori);  // OR_Gate
  buf or_10 (ALUctr[2], lui);  // OR_Gate
endmodule

module Controller (
  input  [5:0] func,
  input  [5:0] op,
  output RegDst,
  output ALUSrc,
  output MemtoRed,
  output RegWrite,
  output MemWrute,
  output branch,
  output ExtOp,
  output [2:0] ALUctr
);

  wire andlogic_1_add, andlogic_1_beq, andlogic_1_lui, andlogic_1_lw, andlogic_1_nop, andlogic_1_ori,
       andlogic_1_sub, andlogic_1_sw;

  andLogic andlogic_1 (
    .add(andlogic_1_add), .ori(andlogic_1_ori), .sub(andlogic_1_sub), .lw(andlogic_1_lw),
    .nop(andlogic_1_nop), .sw(andlogic_1_sw), .beq(andlogic_1_beq), .lui(andlogic_1_lui), .op5(op[5]),
    .op4(op[4]), .op3(op[3]), .op2(op[2]), .op1(op[1]), .op0(op[0]), .func5(func[5]), .func4(func[4]),
    .func3(func[3]), .func2(func[2]), .func1(func[1]), .func0(func[0]));
  orLogic orlogic_1 (
    .RegDst(RegDst), .ALUSrc(ALUSrc), .MemtoRed(MemtoRed), .RegWrite(RegWrite), .MemWrute(MemWrute),
    .branch(branch), .ExtOp(ExtOp), .ALUctr(ALUctr), .add(andlogic_1_add), .sub(andlogic_1_sub),
    .ori(andlogic_1_ori), .lw(andlogic_1_lw), .sw(andlogic_1_sw), .beq(andlogic_1_beq), .lui(andlogic_1_lui),
    .nop(andlogic_1_nop));
endmodule

module NPC (
  input  [31:0] PC,
  input  [15:0] imm,
  input  branch,
  output [31:0] PC_prime
);

  wire [31:0] adder_1_out, bit_extender_1_out, multiplexer_1_out, shifter_1_out;

  assign bit_extender_1_out = {{16{imm[15]}}, imm};  // Bit_Extender bit_extender_1
  Shifter #(.width(32)) shifter_1 (.in(bit_extender_1_out), .\dist (5'b00010), .out(shifter_1_out));
  Adder #(.width(32)) adder_1 (.a(32'h4), .b(PC), .out(adder_1_out));  // open: cin, cout
  Multiplexer #(.width(32)) multiplexer_1 (
    .in0({32{1'b0}}), .in1(shifter_1_out), .out(multiplexer_1_out), .sel(branch));  // open: en
  Adder #(.width(32)) adder_2 (.a(adder_1_out), .b(multiplexer_1_out), .out(PC_prime));  // open: cin, cout
endmodule
