// Logisim project P6.circ as structural Verilog: 26 circuits, main circuit grf_2reg
module grf_2reg (
  input  clk,
  input  reset,
  input  WE,
  input  A1,
  input  A2,
  input  A3,
  input  [31:0] WD,
  output [31:0] RD1,
  output [31:0] RD2
);

  wire A3_0, A3_1, and_1_out, and_2_out;
  wire [31:0] out0, out1;

  Decoder decoder_1 (.out0(A3_0), .out1(A3_1), .sel(A3));  // open: en
  and and_1 (and_1_out, A3_0, WE);
  and and_2 (and_2_out, A3_1, WE);
  Register #(.width(32)) _0 (.D(WD), .en(and_1_out), .Q(out0), .clk(clk), .clr(reset));
  Register #(.width(32)) _1 (.D(WD), .en(and_2_out), .Q(out1), .clk(clk), .clr(reset));
  Multiplexer #(.width(32)) multiplexer_1 (.in0(out0), .in1(out1), .out(RD1), .sel(A1));  // open: en
  Multiplexer #(.width(32)) multiplexer_2 (.in0(out0), .in1(out1), .out(RD2), .sel(A2));  // open: en

  // Other names for the same wires on the sheet: res = reset
endmodule

module grf_4reg (
  input  clk,
  input  reset,
  input  WE,
  input  [1:0] A1,
  input  [1:0] A2,
  input  [1:0] A3,
  input  [31:0] WD,
  output [31:0] RD1,
  output [31:0] RD2
);

  wire A31_0, A31_1, and_1_out, and_2_out;
  wire [31:0] out10, out11, out20, out21;

  Decoder decoder_1 (.out0(A31_0), .out1(A31_1), .sel(A3[1]));  // open: en
  and and_1 (and_1_out, WE, A31_0);
  grf_2reg grf_2reg_1 (
    .A1(A1[0]), .A2(A2[0]), .A3(A3[0]), .WD(WD), .RD1(out10), .RD2(out20), .clk(clk), .reset(reset),
    .WE(and_1_out));
  and and_2 (and_2_out, WE, A31_1);
  grf_2reg grf_2reg_2 (
    .A1(A1[0]), .A2(A2[0]), .A3(A3[0]), .WD(WD), .RD1(out11), .RD2(out21), .clk(clk), .reset(reset),
    .WE(and_2_out));
  Multiplexer #(.width(32)) multiplexer_1 (.in0(out10), .in1(out11), .out(RD1), .sel(A1[1]));  // open: en
  Multiplexer #(.width(32)) multiplexer_2 (.in0(out20), .in1(out21), .out(RD2), .sel(A2[1]));  // open: en

  // Other names for the same wires on the sheet: res = reset
endmodule

module grf_8reg (
  input  clk,
  input  reset,
  input  WE,
  input  [2:0] A1,
  input  [2:0] A2,
  input  [2:0] A3,
  input  [31:0] WD,
  output [31:0] RD1,
  output [31:0] RD2
);

  wire A31_0, A31_1, and_1_out, and_2_out;
  wire [31:0] out10, out11, out20, out21;

  Decoder decoder_1 (.out0(A31_0), .out1(A31_1), .sel(A3[2]));  // open: en
  and and_1 (and_1_out, WE, A31_0);
  grf_4reg grf_4reg_1 (
    .A1(A1[1:0]), .A2(A2[1:0]), .A3(A3[1:0]), .WD(WD), .clk(clk), .reset(reset), .WE(and_1_out), .RD1(out10),
    .RD2(out20));
  and and_2 (and_2_out, WE, A31_1);
  grf_4reg grf_4reg_2 (
    .A1(A1[1:0]), .A2(A2[1:0]), .A3(A3[1:0]), .WD(WD), .clk(clk), .reset(reset), .WE(and_2_out), .RD1(out11),
    .RD2(out21));
  Multiplexer #(.width(32)) multiplexer_1 (.in0(out10), .in1(out11), .out(RD1), .sel(A1[2]));  // open: en
  Multiplexer #(.width(32)) multiplexer_2 (.in0(out20), .in1(out21), .out(RD2), .sel(A2[2]));  // open: en

  // Other names for the same wires on the sheet: A10[1:0] = A1[1:0]; A11 = A1[2]; A20[1:0] = A2[1:0]; A21 = A2[2];
  //   A30[1:0] = A3[1:0]; A31 = A3[2]; res = reset
endmodule

module grf_16reg (
  input  clk,
  input  reset,
  input  WE,
  input  [3:0] A1,
  input  [3:0] A2,
  input  [3:0] A3,
  input  [31:0] WD,
  output [31:0] RD1,
  output [31:0] RD2
);

  wire A31_0, A31_1, and_1_out, and_2_out;
  wire [31:0] out10, out11, out20, out21;

  Decoder decoder_1 (.out0(A31_0), .out1(A31_1), .sel(A3[3]));  // open: en
  and and_1 (and_1_out, WE, A31_0);
  grf_8reg grf_8reg_1 (
    .A1(A1[2:0]), .A2(A2[2:0]), .A3(A3[2:0]), .WD(WD), .clk(clk), .reset(reset), .WE(and_1_out), .RD1(out10),
    .RD2(out20));
  and and_2 (and_2_out, WE, A31_1);
  grf_8reg grf_8reg_2 (
    .A1(A1[2:0]), .A2(A2[2:0]), .A3(A3[2:0]), .WD(WD), .clk(clk), .reset(reset), .WE(and_2_out), .RD1(out11),
    .RD2(out21));
  Multiplexer #(.width(32)) multiplexer_1 (.in0(out10), .in1(out11), .out(RD1), .sel(A1[3]));  // open: en
  Multiplexer #(.width(32)) multiplexer_2 (.in0(out20), .in1(out21), .out(RD2), .sel(A2[3]));  // open: en

  // Other names for the same wires on the sheet: A10[2:0] = A1[2:0]; A11 = A1[3]; A20[2:0] = A2[2:0]; A21 = A2[3];
  //   A30[2:0] = A3[2:0]; A31 = A3[3]; res = reset
endmodule

module grf_32reg (
  input  clk,
  input  reset,
  input  WE,
  input  [4:0] A1,
  input  [4:0] A2,
  input  [4:0] A3,
  input  [31:0] WD,
  output [31:0] RD1,
  output [31:0] RD2
);

  wire A31_0, A31_1, and_1_out, and_2_out;
  wire [31:0] out10, out11, out20, out21;

  Decoder decoder_1 (.out0(A31_0), .out1(A31_1), .sel(A3[4]));  // open: en
  and and_1 (and_1_out, WE, A31_0);
  grf_16reg grf_16reg_1 (
    .A1(A1[3:0]), .A2(A2[3:0]), .A3(A3[3:0]), .WD(WD), .clk(clk), .reset(reset), .WE(and_1_out), .RD1(out10),
    .RD2(out20));
  and and_2 (and_2_out, WE, A31_1);
  grf_16reg grf_16reg_2 (
    .A1(A1[3:0]), .A2(A2[3:0]), .A3(A3[3:0]), .WD(WD), .clk(clk), .reset(reset), .WE(and_2_out), .RD1(out11),
    .RD2(out21));
  Multiplexer #(.width(32)) multiplexer_1 (.in0(out10), .in1(out11), .out(RD1), .sel(A1[4]));  // open: en
  Multiplexer #(.width(32)) multiplexer_2 (.in0(out20), .in1(out21), .out(RD2), .sel(A2[4]));  // open: en

  // Other names for the same wires on the sheet: A10[3:0] = A1[3:0]; A11 = A1[4]; A20[3:0] = A2[3:0]; A21 = A2[4];
  //   A30[3:0] = A3[3:0]; A31 = A3[4]; res = reset
endmodule

module GRF (
  input  clk,
  input  reset,
  input  WE,
  input  [4:0] A1,
  input  [4:0] A2,
  input  [4:0] A3,
  input  [31:0] WD,
  output [31:0] RD1,
  output [31:0] RD2
);

  wire comparator_1_eq;
  wire [31:0] WD_t;

  Comparator #(.width(5)) comparator_1 (.a({5{1'b0}}), .b(A3), .eq(comparator_1_eq));  // open: gt, lt
  Multiplexer #(.width(32)) multiplexer_1 (.in0(WD), .in1({32{1'b0}}), .out(WD_t), .sel(comparator_1_eq));  // open: en
  grf_32reg grf_32reg_1 (.A1(A1), .A2(A2), .A3(A3), .WD(WD_t), .clk(clk), .reset(reset), .WE(WE), .RD1(RD1), .RD2(RD2));

  // Other names for the same wires on the sheet: res = reset
endmodule

module IM (
  input  [31:0] PC,
  output [31:0] Instr
);

  wire [31:0] subtractor_1_out;

  Subtractor #(.width(32)) subtractor_1 (.a(PC), .b(32'h3000), .out(subtractor_1_out));  // open: bin, bout
  ROM #(.addrWidth(12), .dataWidth(32)) rom_1 (.addr(subtractor_1_out[13:2]), .data(Instr));  // open: sel

  // Notes on the sheet:
  //   IM
  //   contents of rom_1 (hex, n*v repeats v):
  //   3404007b 348501c8 3c06007b 3c07ffff 34e7ffff 868020 878820 e79020 34080000 ad040000 ad050004
  //   ad060008 ad07000c ad100010 ad110014 ad120018 8d040000 8d05000c ad04001c ad050020 34040001 34050002
  //   34060001 10850001 10860001 ad040024 ad050028
endmodule

module ALU (
  input  [31:0] Op1,
  input  [31:0] Op2,
  input  [2:0] ALUControl,
  output [31:0] ALUResult,
  output Zero
);

  wire comparator_1_lt;
  wire [31:0] adder_1_out, bit_extender_1_out, or_1_out, shifter_1_out, subtractor_1_out;

  Adder #(.width(32)) adder_1 (.a(Op1), .b(Op2), .out(adder_1_out));  // open: cin, cout
  Subtractor #(.width(32)) subtractor_1 (.a(Op1), .b(Op2), .out(subtractor_1_out));  // open: bin, bout
  assign or_1_out = Op1 | Op2;  // OR_Gate or_1, 32 bits wide
  Comparator #(.width(32), .mode("unsigned")) comparator_1 (.a(Op1), .b(Op2), .lt(comparator_1_lt));  // open: gt, eq
  Shifter #(.width(32)) shifter_1 (.in(Op2), .\dist (5'b10000), .out(shifter_1_out));
  assign bit_extender_1_out = {{31{1'b0}}, comparator_1_lt};  // Bit_Extender bit_extender_1
  Multiplexer #(.select(3), .width(32)) multiplexer_1 (
    .in0(adder_1_out), .in1(subtractor_1_out), .in2(or_1_out), .in3(bit_extender_1_out), .in4(shifter_1_out),
    .out(ALUResult), .sel(ALUControl));  // open: in5, in6, in7, en
  Comparator #(.width(32), .mode("unsigned")) comparator_2 (.a(ALUResult), .b({32{1'b0}}), .eq(Zero));  // open: gt, lt
endmodule

module andLogic (
  input  op5,
  input  op4,
  input  op3,
  input  op2,
  input  op1,
  input  op0,
  input  func5,
  input  func4,
  input  func3,
  input  func2,
  input  func1,
  input  func0,
  output add,
  output ori,
  output sub,
  output lw,
  output nop,
  output sw,
  output jr,
  output beq,
  output lui,
  output jal
);

  wire a_s_n, not_1_out, not_2_out, not_3_out, not_4_out, not_5_out, not_6_out, not_7_out, not_8_out,
       not_9_out, not_10_out, not_11_out, not_12_out;

  not not_1 (not_1_out, op5);
  not not_2 (not_2_out, op4);
  not not_3 (not_3_out, op2);
  not not_4 (not_4_out, op3);
  not not_5 (not_5_out, op0);
  not not_6 (not_6_out, op1);
  and u_a_s_n (a_s_n, not_1_out, not_2_out, not_4_out, not_3_out, not_6_out, not_5_out);
  and u_ori (ori, not_1_out, not_2_out, op3, op2, not_6_out, op0);
  and u_lw (lw, op5, not_2_out, not_4_out, not_3_out, op1, op0);
  and u_sw (sw, op5, not_2_out, op3, not_3_out, op1, op0);
  and u_beq (beq, not_1_out, not_2_out, not_4_out, op2, not_6_out, not_5_out);
  and u_lui (lui, not_1_out, not_2_out, op3, op2, op1, op0);
  and u_jal (jal, not_1_out, not_2_out, not_4_out, not_3_out, op1, op0);
  not not_7 (not_7_out, func5);
  not not_8 (not_8_out, func4);
  not not_9 (not_9_out, func2);
  not not_10 (not_10_out, func3);
  not not_11 (not_11_out, func1);
  not not_12 (not_12_out, func0);
  and u_add (add, a_s_n, func5, not_8_out, not_10_out, not_9_out, not_11_out, not_12_out);
  and u_sub (sub, a_s_n, func5, not_8_out, not_10_out, not_9_out, func1, not_12_out);
  and u_nop (nop, a_s_n, not_7_out, not_8_out, not_10_out, not_9_out, not_11_out, not_12_out);
  and u_jr (jr, a_s_n, not_7_out, not_8_out, func3, not_9_out, not_11_out, not_12_out);
endmodule

module DM (
  input  clk,
  input  reset,
  input  [1:0] WE,
  input  [31:0] A,
  input  [31:0] WD,
  output [31:0] RD
);

  wire [1:0] sel;
  wire [9:0] A00, A01, A10, A_t;
  wire [15:0] bit_extender_1_out;
  wire [31:0] ram_1_data, ram_2_data, ram_3_data;

  Demultiplexer #(.select(2), .width(10)) demultiplexer_1 (
    .out0(A00), .out1(A01), .out2(A10), .in(A_t), .sel(sel));  // open: out3, en
  Bit_Extender #(.in_width(32)) bit_extender_1 (
    .in(A), .out({bit_extender_1_out[15:14], sel, A_t, bit_extender_1_out[1:0]}));
  RAM #(.addrWidth(10), .dataWidth(32), .bus("separate")) ram_1 (
    .addr(A00), .din(WD), .data(ram_1_data), .str(WE[0]), .clk(clk), .clr(reset));  // open: sel, ld
  RAM #(.addrWidth(10), .dataWidth(32), .bus("separate")) ram_2 (
    .addr(A01), .din(WD), .data(ram_2_data), .str(WE[0]), .clk(clk), .clr(reset));  // open: sel, ld
  RAM #(.addrWidth(10), .dataWidth(32), .bus("separate")) ram_3 (
    .addr(A10), .din(WD), .data(ram_3_data), .str(WE[0]), .clk(clk), .clr(reset));  // open: sel, ld
  Multiplexer #(.select(2), .width(32)) multiplexer_1 (
    .in0(ram_1_data), .in1(ram_2_data), .in2(ram_3_data), .out(RD), .sel(sel));  // open: in3, en
  // Pins of 1 and 2 bits meet at WE

  // Other names for the same wires on the sheet: res = reset
endmodule

module EXT (
  input  [1:0] A,
  input  [31:0] Din,
  input  [2:0] Op,
  output [31:0] Dout
);
endmodule

module orLogic (
  input  add,
  input  sub,
  input  ori,
  input  lw,
  input  sw,
  input  beq,
  input  lui,
  input  nop,
  input  jal,
  input  jr,
  output [1:0] MemtoReg,
  output RegWrite,
  output MemWrite,
  output MemRead,
  output [1:0] branch,
  output [2:0] ALUctr,
  output ALUSrc,
  output [1:0] RegDst
);

  buf or_1 (MemtoReg[0], jal);  // OR_Gate
  or or_2 (MemtoReg[1], add, sub, ori, lui);
  or or_3 (RegWrite, add, sub, ori, lw, lui, jal);
  buf or_4 (MemWrite, sw);  // OR_Gate
  buf or_5 (MemRead, lw);  // OR_Gate
  or or_6 (branch[0], beq, jr);
  buf or_7 (branch[1], jal);  // OR_Gate
  or or_8 (ALUctr[0], sub, beq, lui);
  or or_9 (ALUctr[1], ori, lui);
  buf or_10 (ALUctr[2], 1'b0);  // OR_Gate
  or or_11 (ALUSrc, ori, lw, sw, lui);
  or or_12 (RegDst[0], add, sub);
  buf or_13 (RegDst[1], jal);  // OR_Gate
endmodule

module Controller (
  input  [5:0] func,
  input  [5:0] op,
  output [1:0] MemtoRed,
  output RegWrite,
  output [1:0] MemWrite,
  output [1:0] branch,
  output [2:0] ALUctr,
  output ALUSrc,
  output [1:0] RegDst
);

  wire andlogic_1_add, andlogic_1_beq, andlogic_1_jal, andlogic_1_jr, andlogic_1_lui, andlogic_1_lw,
       andlogic_1_nop, andlogic_1_ori, andlogic_1_sub, andlogic_1_sw;

  andLogic andlogic_1 (
    .add(andlogic_1_add), .ori(andlogic_1_ori), .sub(andlogic_1_sub), .lw(andlogic_1_lw),
    .nop(andlogic_1_nop), .sw(andlogic_1_sw), .beq(andlogic_1_beq), .lui(andlogic_1_lui), .op5(op[5]),
    .op4(op[4]), .op3(op[3]), .op2(op[2]), .op1(op[1]), .op0(op[0]), .func5(func[5]), .func4(func[4]),
    .func3(func[3]), .func2(func[2]), .func1(func[1]), .func0(func[0]), .jr(andlogic_1_jr),
    .jal(andlogic_1_jal));
  orLogic orlogic_1 (
    .RegDst(RegDst), .ALUSrc(ALUSrc), .MemtoReg(MemtoRed), .RegWrite(RegWrite), .MemWrite(MemWrite[0]),
    .branch(branch), .ALUctr(ALUctr), .add(andlogic_1_add), .sub(andlogic_1_sub), .ori(andlogic_1_ori),
    .lw(andlogic_1_lw), .sw(andlogic_1_sw), .beq(andlogic_1_beq), .lui(andlogic_1_lui), .nop(andlogic_1_nop),
    .jal(andlogic_1_jal), .jr(andlogic_1_jr));  // open: MemRead
  // Pins of 1 and 2 bits meet at MemWrite
endmodule

module main (
  input  [31:0] i_inst_rdata,
  input  [31:0] m_data_rdata,
  input  in_3,
  input  in_4,
  output w_grf_we,
  output [31:0] i_inst_addr,
  output [3:0] m_data_byteen,
  output [31:0] m_data_addr,
  output [31:0] m_data_wdata,
  output [31:0] w_grf_wdata,
  output [31:0] w_inst_addr,
  output [4:0] w_grf_addr,
  output [31:0] m_inst_addr
);

  wire comparator_1_eq, controller_1_alusrc, controller_1_regwrite, ex_1_out_7, hazardctrl_1_out_5,
       hazardctrl_1_out_6, hazardctrl_1_out_7, hazardctrl_1_out_8, hazardctrl_1_out_9, id_ex_1_p14,
       not_1_out, not_2_out, rst, undriven, wb_1_out_6, wb_2_out_6;
  wire [1:0] controller_1_branch, controller_1_memtored, controller_1_memwrite, controller_1_regdst,
       ex_1_out_8, m_1_out_4, m_2_out_4, undriven_2, wb_1_out_5, wb_2_out_5, wb_3_out_5;
  wire [2:0] controller_1_aluctr, ex_1_out_6;
  wire [4:0] ex_mem_1_out_12, id_ex_1_p11, id_ex_1_p12, if_id_1_out_9, if_id_1_out_10, if_id_1_out_12,
       if_id_1_out_13, if_id_1_out_14, multiplexer_8_out;
  wire [5:0] if_id_1_func, if_id_1_opcode;
  wire [15:0] if_id_1_out_11;
  wire [25:0] if_id_1_out_15;
  wire [31:0] adder_1_out, adder_2_out, alu_1_aluresult, bit_extender_1_out, ex_mem_1_gpr_rt_2,
       ex_mem_1_pc_prime, ext_2_dout, grf_1_rd1, grf_1_rd2, id_ex_1_p8, id_ex_1_p9, id_ex_1_p10, id_ex_1_p13,
       if_id_1_pc_prime, instr_1_out_2, instr_2_out_2, instr_3_out_2, instr_4_out_2, mem_wb_1_p5,
       mem_wb_1_p6, mem_wb_1_p8, multiplexer_1_out, multiplexer_2_out, multiplexer_3_out, multiplexer_4_out,
       multiplexer_5_out, multiplexer_6_out, multiplexer_7_out, multiplexer_9_out, npc_1_npc, undriven_3,
       undriven_4, undriven_5;

  Multiplexer #(.select(2), .width(32)) multiplexer_1 (
    .in0(adder_1_out), .in1(npc_1_npc), .in2(npc_1_npc), .in3(multiplexer_2_out), .out(multiplexer_1_out),
    .sel(controller_1_branch));  // open: en
  not not_1 (not_1_out, hazardctrl_1_out_6);
  PC pc_1 (.PC_prime(multiplexer_1_out), .PC(i_inst_addr), .EN(not_1_out));  // open: clk, rst
  Adder #(.width(32)) adder_1 (.a(i_inst_addr), .b(32'h4), .out(adder_1_out));  // open: cin, cout
  IM im_1 ();  // open: Instr, PC
  IF_ID if_id_1 (
    .RD(i_inst_rdata), .PC(adder_1_out), .PC_prime(if_id_1_pc_prime), .WE(not_2_out),
    .OpCode(if_id_1_opcode), .Func(if_id_1_func), .out_9(if_id_1_out_9), .out_10(if_id_1_out_10),
    .out_11(if_id_1_out_11), .out_12(if_id_1_out_12), .out_13(if_id_1_out_13), .out_14(if_id_1_out_14),
    .out_15(if_id_1_out_15));  // open: clk, rst
  not not_2 (not_2_out, undriven);
  Instr instr_1 (.in_1(i_inst_rdata), .out_2(instr_1_out_2));
  HazardCtrl hazardctrl_1 (
    .out_5(hazardctrl_1_out_5), .in_2(instr_2_out_2), .out_6(hazardctrl_1_out_6), .in_3(instr_3_out_2),
    .out_8(hazardctrl_1_out_8), .in_4(instr_4_out_2), .out_9(hazardctrl_1_out_9), .out_7(hazardctrl_1_out_7));  // open: in_1
  Controller controller_1 (
    .RegDst(controller_1_regdst), .ALUSrc(controller_1_alusrc), .MemtoRed(controller_1_memtored),
    .RegWrite(controller_1_regwrite), .MemWrite(controller_1_memwrite), .branch(controller_1_branch),
    .ALUctr(controller_1_aluctr), .op(if_id_1_opcode), .func(if_id_1_func));
  GRF grf_1 (
    .A1(if_id_1_out_9), .A2(if_id_1_out_10), .A3(w_grf_addr), .WD(w_grf_wdata), .RD1(grf_1_rd1),
    .RD2(grf_1_rd2), .clk(in_3), .reset(rst), .WE(w_grf_we));
  assign bit_extender_1_out = {{16{if_id_1_out_11[15]}}, if_id_1_out_11};  // Bit_Extender bit_extender_1
  NPC npc_1 (.PC(if_id_1_pc_prime), .Imm26(if_id_1_out_15), .NPC(npc_1_npc), .in_3(undriven_2), .in_1(comparator_1_eq));
  Multiplexer #(.select(2), .width(32)) multiplexer_2 (
    .in0(grf_1_rd1), .in1(w_grf_wdata), .in2(multiplexer_9_out), .out(multiplexer_2_out));  // open: in3, sel, en
  Multiplexer #(.select(2), .width(32)) multiplexer_3 (
    .in0(grf_1_rd2), .in1(w_grf_wdata), .in2(multiplexer_9_out), .out(multiplexer_3_out));  // open: in3, sel, en
  WB wb_1 (
    .in_3(controller_1_memtored), .in_4(controller_1_regwrite), .out_5(wb_1_out_5), .out_6(wb_1_out_6));  // open: clk, rst
  M m_1 (.in_3(controller_1_memwrite), .out_4(m_1_out_4));  // open: clk, rst
  EX ex_1 (
    .in_3(controller_1_aluctr), .in_4(controller_1_alusrc), .in_5(controller_1_regdst), .out_6(ex_1_out_6),
    .out_7(ex_1_out_7), .out_8(ex_1_out_8));  // open: clk, rst
  // ID_EX id_ex_1: pin names not known; wires that end beside it: multiplexer_2_out, multiplexer_3_out, bit_extender_1_out, if_id_1_out_12, if_id_1_out_13, if_id_1_out_14, if_id_1_pc_prime, id_ex_1_p8, id_ex_1_p9, id_ex_1_p10, id_ex_1_p11, id_ex_1_p12, id_ex_1_p13, id_ex_1_p14
  Instr instr_2 (.in_1(instr_1_out_2), .out_2(instr_2_out_2));
  Multiplexer #(.select(2), .width(32)) multiplexer_4 (
    .in0(id_ex_1_p8), .in1(w_grf_wdata), .in2(multiplexer_9_out), .out(multiplexer_4_out));  // open: in3, sel, en
  Multiplexer #(.select(2), .width(32)) multiplexer_5 (
    .in0(id_ex_1_p9), .in1(w_grf_wdata), .in2(multiplexer_9_out), .out(multiplexer_5_out));  // open: in3, sel, en
  Comparator #(.width(32), .mode("unsigned")) comparator_1 (
    .a(multiplexer_3_out), .b(multiplexer_2_out), .eq(comparator_1_eq));  // open: gt, lt
  Multiplexer #(.width(32)) multiplexer_6 (
    .in0(multiplexer_5_out), .in1(id_ex_1_p10), .out(multiplexer_6_out));  // open: sel, en
  HILO hilo_1 (.out_3(multiplexer_4_out), .out_4(multiplexer_6_out), .in_1(undriven_3), .in_2(undriven_4));
  Multiplexer #(.width(32)) multiplexer_7 (
    .in0(undriven_3), .in1(undriven_4), .out(multiplexer_7_out));  // open: sel, en
  Multiplexer #(.select(2), .width(5)) multiplexer_8 (
    .in0(id_ex_1_p11), .in1(id_ex_1_p12), .in2(5'b10001), .out(multiplexer_8_out));  // open: in3, sel, en
  WB wb_2 (.in_3(wb_1_out_5), .in_4(wb_1_out_6), .out_5(wb_2_out_5), .out_6(wb_2_out_6));  // open: clk, rst
  M m_2 (.in_3(m_1_out_4), .out_4(m_2_out_4));  // open: clk, rst
  ALU alu_1 (.ALUResult(alu_1_aluresult), .Op1(multiplexer_4_out), .Op2(multiplexer_6_out));  // open: ALUControl, Zero
  EX_MEM ex_mem_1 (
    .ALUResult(alu_1_aluresult), .GPR_rt(multiplexer_5_out), .in_4(multiplexer_8_out), .PC(id_ex_1_p13),
    .ALUResult_2(m_data_addr), .GPR_rt_2(ex_mem_1_gpr_rt_2), .out_12(ex_mem_1_out_12),
    .PC_prime(ex_mem_1_pc_prime));  // open: clk, rst, WE, in_1, out_9
  Instr instr_3 (.in_1(instr_2_out_2), .out_2(instr_3_out_2));
  EXT ext_1 (.Din(ex_mem_1_gpr_rt_2), .Dout(m_data_wdata));  // open: A, Op
  Subtractor #(.width(32)) subtractor_1 (.a(ex_mem_1_pc_prime), .b(32'h4), .out(m_inst_addr));  // open: bin, bout
  Multiplexer #(.width(32)) multiplexer_9 (
    .in0(m_data_addr), .in1(undriven_5), .out(multiplexer_9_out));  // open: sel, en
  Instr instr_4 (.in_1(instr_3_out_2), .out_2(instr_4_out_2));
  DM dm_1 ();  // open: A, WD, RD, clk, reset, WE
  EXT ext_2 (.Din(m_data_rdata), .Dout(ext_2_dout));  // open: A, Op
  Adder #(.width(32)) adder_2 (.a(ex_mem_1_pc_prime), .b(32'h4), .out(adder_2_out));  // open: cin, cout
  WB wb_3 (.in_3(wb_2_out_5), .in_4(wb_2_out_6), .out_5(wb_3_out_5), .out_6(w_grf_we));  // open: clk, rst
  // MEM_WB mem_wb_1: pin names not known; wires that end beside it: ext_2_dout, multiplexer_9_out, ex_mem_1_out_12, adder_2_out, mem_wb_1_p5, mem_wb_1_p6, w_grf_addr, mem_wb_1_p8
  Multiplexer #(.select(2), .width(32)) multiplexer_10 (
    .in0(mem_wb_1_p5), .in1(mem_wb_1_p6), .in2(mem_wb_1_p8), .out(w_grf_wdata));  // open: in3, sel, en
  Subtractor #(.width(32)) subtractor_2 (.a(mem_wb_1_p8), .b(32'h8), .out(w_inst_addr));  // open: bin, bout

  // Other names for the same wires on the sheet: clk = in_3; reset = in_4

  // Notes on the sheet:
  //   PCSel
  //   0:PC+4
  //   1:beq
  //   2:jal
  //   3:jr
  //   StallPC
  //   F
  //   31:26
  //   5:0
  //   20:16
  //   15:0
  //   15:11
  //   PC
  //   25:0
  //   D
  //   25:21
  //   Rs
  //   Rt
  //   Imm16
  //   25:21
  //   20:16
  //   Instr_D
  //   StallD
  //   0:GPR[rs/rt]
  //   1:WD_W
  //   2:AO_M
  //   PCSel
  //   RD1_D_Sel
  //   D
  //   RD1_D_Sel
  //   RD1_D
  //   RD2_D
  //   RD2_D_Sel
  //   Imm32
  //   Rs
  //   Rt
  //   Rd
  //   RD1_D
  //   GPR[rs]=GPR[rt]
  //   RD2_D_Sel
  //   WDSel
  //   RegWrite
  //   MenWrite
  //   RegDst
  //   ALUSrc
  //   ALUCtrl
  //   PC
  //   E
  //   ClrE
  //   HazardCtrl
  //   RegWrite_E
  //   RD1_E_Sel
  //   RD2_E_Sel
  //   ALUSrc
  //   M/D
  //   Start
  //   HILOCtrl
  //   0:rt
  //   1:rd
  //   2:$31, jr
  //   RD1_E_Sel
  //   Instr_E
  //   RegWrite_E
  //   E
  //   ALUCtrl
  //   0:GPR[rt]
  //   1:Imm
  //   HILOSel
  //   RegDst
  //   RD2_E_Sel
  //   RegDst_E
  //   WDSel
  //   GPR[rt]
  //   PC
  //   Instr_M
  //   M
  //   RegWrite
  //   MenWrite
  //   ExtOp
  //   RegWrite_M
  //   AOSel
  //   W
  //   RegDst_M
  //   RegWrite_M
  //   GPR_A3
  //   Instr_W
  //   RegDst_W
  //   RegWrite_W
  //   M
  //   ExtOp
  //   WDSel
  //   0:Memory[AO]
  //   1:AO
  //   2:PC+8
  //   PC
  //   W
  //   WDSel
  //   GPR_WD
endmodule

module PC (
  input  [31:0] PC_prime,
  input  clk,
  input  rst,
  input  EN,
  output [31:0] PC
);

  wire counter_1_q;
  wire [31:0] multiplexer_1_out;

  Multiplexer #(.width(32)) multiplexer_1 (
    .in0(32'h3000), .in1(PC_prime), .out(multiplexer_1_out), .sel(counter_1_q));  // open: en
  Counter #(.width(1), .max('h1), .ongoal("stay")) counter_1 (
    .Q(counter_1_q), .clk(clk), .clr(rst));  // open: load, D, count, carry
  Register #(.width(32)) u_PC (.D(multiplexer_1_out), .en(EN), .Q(PC), .clk(clk), .clr(rst));
endmodule

module IF_ID (
  input  [31:0] PC,
  input  [31:0] RD,
  input  clk,
  input  rst,
  input  WE,
  output [31:0] PC_prime,
  output [5:0] OpCode,
  output [5:0] Func,
  output [4:0] out_9,
  output [4:0] out_10,
  output [15:0] out_11,
  output [4:0] out_12,
  output [4:0] out_13,
  output [4:0] out_14,
  output [25:0] out_15
);

  Register #(.width(32)) register_1 (.D(PC), .en(WE), .Q(PC_prime), .clk(clk), .clr(rst));
  Register #(.width(32)) register_2 (
    .D(RD), .en(WE), .Q({OpCode, out_9, out_10, out_11[15:6], Func}), .clk(clk), .clr(rst));

  assign out_11[5:0] = Func;
  assign out_12 = out_9;
  assign out_13 = out_10;
  assign out_14 = out_11[15:11];
  assign out_15 = {out_9, out_10, out_11[15:6], Func};
endmodule

module ID_EX (
  input  [31:0] in_1,
  input  [31:0] in_2,
  input  [31:0] in_3,
  input  [31:0] in_4,
  input  [4:0] in_5,
  input  [4:0] in_6,
  input  clk,
  input  rst,
  input  [4:0] in_9,
  input  WE,
  output [31:0] out_11,
  output [31:0] out_12,
  output [31:0] out_13,
  output [31:0] out_14,
  output [4:0] out_15,
  output [4:0] out_16,
  output [4:0] out_17
);

  Register #(.width(32)) register_1 (.D(in_1), .en(WE), .Q(out_11), .clk(clk), .clr(rst));
  Register #(.width(32)) register_2 (.D(in_2), .en(WE), .Q(out_12), .clk(clk), .clr(rst));
  Register #(.width(32)) register_3 (.D(in_3), .en(WE), .Q(out_13), .clk(clk), .clr(rst));
  Register #(.width(32)) register_4 (.D(in_4), .en(WE), .Q(out_14), .clk(clk), .clr(rst));
  Register #(.width(5)) register_5 (.D(in_5), .en(WE), .Q(out_15), .clk(clk), .clr(rst));
  Register #(.width(5)) register_6 (.D(in_6), .en(WE), .Q(out_16), .clk(clk), .clr(rst));
  Register #(.width(5)) register_7 (.D(in_9), .en(WE), .Q(out_17), .clk(clk), .clr(rst));
endmodule

module NPC (
  input  in_1,
  input  [25:0] Imm26,
  input  [1:0] in_3,
  input  [31:0] PC,
  output [31:0] NPC
);

  wire [15:0] shifter_1_out;
  wire [31:0] adder_1_out, bit_extender_1_out, multiplexer_1_out, subtractor_1_out;

  Subtractor #(.width(32)) subtractor_1 (.a(PC), .b(32'h4), .out(subtractor_1_out));  // open: bin, bout
  Shifter #(.width(16)) shifter_1 (.in(Imm26[15:0]), .\dist (4'b0010), .out(shifter_1_out));
  assign bit_extender_1_out = {{16{1'b0}}, shifter_1_out};  // Bit_Extender bit_extender_1
  Adder #(.width(32)) adder_1 (.a(bit_extender_1_out), .b(PC), .out(adder_1_out));  // open: cin, cout
  Multiplexer #(.width(32)) multiplexer_1 (
    .in0(PC), .in1(adder_1_out), .out(multiplexer_1_out), .sel(in_1));  // open: en
  Multiplexer #(.select(2), .width(32)) multiplexer_2 (
    .in1(multiplexer_1_out), .in2({subtractor_1_out[31:28], Imm26, 2'b00}), .out(NPC), .sel(in_3));  // open: in0, in3, en
endmodule

module EX_MEM (
  input  in_1,
  input  [31:0] ALUResult,
  input  [31:0] GPR_rt,
  input  [4:0] in_4,
  input  [31:0] PC,
  input  clk,
  input  rst,
  input  WE,
  output out_9,
  output [31:0] ALUResult_2,
  output [31:0] GPR_rt_2,
  output [4:0] out_12,
  output [31:0] PC_prime
);

  Register #(.width(1)) register_1 (.D(in_1), .en(WE), .Q(out_9), .clk(clk), .clr(rst));
  Register #(.width(32)) register_2 (.D(ALUResult), .en(WE), .Q(ALUResult_2), .clk(clk), .clr(rst));
  Register #(.width(32)) register_3 (.D(GPR_rt), .en(WE), .Q(GPR_rt_2), .clk(clk), .clr(rst));
  Register #(.width(5)) register_4 (.D(in_4), .en(WE), .Q(out_12), .clk(clk), .clr(rst));
  Register #(.width(32)) register_5 (.D(PC), .en(WE), .Q(PC_prime), .clk(clk), .clr(rst));
endmodule

module MEM_WB (
  input  [31:0] RD,
  input  [31:0] ALUResult,
  input  [31:0] PC,
  input  [4:0] in_4,
  input  clk,
  input  rst,
  input  WE,
  output [31:0] RD_2,
  output [31:0] ALUResult_2,
  output [31:0] PC_prime,
  output [4:0] out_11
);

  Register #(.width(32)) register_1 (.D(RD), .en(WE), .Q(RD_2), .clk(clk), .clr(rst));
  Register #(.width(32)) register_2 (.D(ALUResult), .en(WE), .Q(ALUResult_2), .clk(clk), .clr(rst));
  Register #(.width(32)) register_3 (.D(PC), .en(WE), .Q(PC_prime), .clk(clk), .clr(rst));
  Register #(.width(5)) register_4 (.D(in_4), .en(WE), .Q(out_11), .clk(clk), .clr(rst));
endmodule

module EX (
  input  clk,
  input  rst,
  input  [2:0] in_3,
  input  in_4,
  input  [1:0] in_5,
  output [2:0] out_6,
  output out_7,
  output [1:0] out_8
);

  Register #(.width(3)) register_1 (.D(in_3), .Q(out_6), .clk(clk), .clr(rst));  // open: en
  Register #(.width(1)) register_2 (.D(in_4), .Q(out_7), .clk(clk), .clr(rst));  // open: en
  Register #(.width(2)) register_3 (.D(in_5), .Q(out_8), .clk(clk), .clr(rst));  // open: en
endmodule

module M (
  input  clk,
  input  rst,
  input  [1:0] in_3,
  output [1:0] out_4
);

  wire register_1_q, register_2_q, undriven;

  Register #(.width(1)) register_1 (.Q(register_1_q), .clk(clk), .clr(rst));  // open: D, en
  Register #(.width(1)) register_2 (.D(undriven), .Q(register_2_q), .clk(clk), .clr(rst));  // open: en
  Register #(.width(2)) register_3 (.D(in_3), .Q(out_4), .clk(clk), .clr(rst));  // open: en
endmodule

module WB (
  input  clk,
  input  rst,
  input  [1:0] in_3,
  input  in_4,
  output [1:0] out_5,
  output out_6
);

  Register #(.width(2)) register_1 (.D(in_3), .Q(out_5), .clk(clk), .clr(rst));  // open: en
  Register #(.width(1)) register_2 (.D(in_4), .Q(out_6), .clk(clk), .clr(rst));  // open: en
endmodule

module Instr (
  input  [31:0] in_1,
  output [31:0] out_2
);
endmodule

module HazardCtrl (
  input  [31:0] in_1,
  input  [31:0] in_2,
  input  [31:0] in_3,
  input  [31:0] in_4,
  output out_5,
  output out_6,
  output out_7,
  output out_8,
  output out_9
);
endmodule

module HILO (
  input  [31:0] in_1,
  input  [31:0] in_2,
  output [31:0] out_3,
  output [31:0] out_4
);
endmodule
